// Logisim project NOR, NAND, NAND, XNOR, XOR.circ as structural Verilog: 1 circuit, main circuit main
module main (
  input  A,
  input  B,
  input  C,
  input  D,
  output Y,
  output Z,
  output DNF_Y,
  output DNF_Z,
  output KNF_Y,
  output KNF_Z
);

  wire AC_nD_out, B_nD_out, BC_nD_out, BD_out, C_nD_out, D_C_out, n_A_B_out, n_B_D_out, n_C_D_out, nA_C_out,
       nA_nB_nC_out, nA_nBD_out, nA_nD_out, nB_C_out, nB_nD_out, not_1_out, not_2_out, not_3_out, not_4_out,
       not_5_out, or_1_out;

  not not_1 (not_1_out, D);
  not not_2 (not_2_out, A);
  not not_3 (not_3_out, B);
  not not_4 (not_4_out, C);
  not not_5 (not_5_out, D);
  nor n_A_B (n_A_B_out, A, B);
  nand n_C_D (n_C_D_out, C, not_1_out);
  nand n_B_D (n_B_D_out, B, D);
  xor xor_1 (Z, n_C_D_out, n_B_D_out);
  and nA_nB_nC (nA_nB_nC_out, not_2_out, not_3_out, not_4_out);
  and nA_nBD (nA_nBD_out, not_2_out, not_3_out, D);
  and AC_nD (AC_nD_out, A, C, not_5_out);
  and BC_nD (BC_nD_out, B, C, not_2_out);
  and BD (BD_out, B, D);
  and C_nD (C_nD_out, C, not_2_out);
  xnor xnor_1 (Y, n_A_B_out, n_C_D_out);
  or OR_Y (DNF_Y, nA_nB_nC_out, nA_nBD_out, AC_nD_out, BC_nD_out);
  or OR_Z (DNF_Z, BD_out, C_nD_out);
  or nA_C (nA_C_out, not_2_out, C);
  or nA_nD (nA_nD_out, not_2_out, not_5_out);
  or nB_C (nB_C_out, not_3_out, C);
  or nB_nD (nB_nD_out, not_5_out, not_3_out);
  or or_1 (or_1_out, not_4_out, D, A, B);
  or B_nD (B_nD_out, B, not_5_out);
  or D_C (D_C_out, D, C);
  and AND_Y (KNF_Y, nA_C_out, nA_nD_out, nB_C_out, nB_nD_out, or_1_out);
  and AND_Z (KNF_Z, B_nD_out, D_C_out);

  // Notes on the sheet:
  //   Negácia D
  //   !C
  //   !D
  //   Zadaná schéma
  //   !A
  //   !B
  //   (!(A+B)+!(!(C!D)))*(!(!(A+B))+!(C!D)) 
  //   (!(C!D) !(!(BD))) + (!(!(C!D)) !(BD)) 
  //   DNF
  //   !C+D+A+B
  //   KNF
endmodule
