// Logisim project 2_zad_opravena.circ as structural Verilog: 1 circuit, main circuit main
module main (
  input  a,
  input  b,
  input  c,
  input  d,
  output A_D,
  output B_D,
  output C_D,
  output D_D,
  output A_K,
  output B_K,
  output C_K,
  output D_K
);

  wire n_a_b_c_out, n_a_b_out, n_a_c_d_out, n_a_c_nd_out, n_b_c_out, n_b_nc_d_out, n_b_nd_out, n_nb_c_out,
       n_nb_nc_out, na_out, nb_2_out, nb_out, nc_2_out, nc_out, nd_2_out, nd_out;

  nand na (na_out, a, a);
  nand nb (nb_out, b, b);
  nand nc (nc_out, c, c);
  nor nb_2 (nb_2_out, b, b);
  nor nc_2 (nc_2_out, c, c);
  nand nd (nd_out, d, d);
  nor nd_2 (nd_2_out, d, d);
  nand n_b_c (n_b_c_out, b, c);
  nand n_b_nc_d (n_b_nc_d_out, b, d, nc_out);
  nand n_b_nd (n_b_nd_out, b, nd_out);
  nand n_nb_c (n_nb_c_out, nb_out, c);
  nor n_a_c_d (n_a_c_d_out, a, c, d);
  nor n_a_b (n_a_b_out, a, b);
  nor n_a_c_nd (n_a_c_nd_out, a, nd_2_out, c);
  nor n_nb_nc (n_nb_nc_out, nb_2_out, nc_2_out);
  nor n_a_b_c (n_a_b_c_out, a, b, c);
  nand n_na_n_b_c__n_b_nc_d (A_D, na_out, n_b_c_out, n_b_nc_d_out);
  nand n_na_n_b_c__n_b_nd (B_D, n_b_c_out, n_b_nd_out, na_out);
  nand n_na_n_b_nc_d__n_nb_c (C_D, n_b_nc_d_out, na_out, n_nb_c_out);
  nor n_n_a_c_d__n_a_b (A_K, n_a_c_d_out, n_a_b_out);
  nor n_n_a_b__n_a_c_nd (B_K, n_a_b_out, n_a_c_nd_out);
  nor n_n_a_c_d__n_nb_nc__n_a_b_c (C_K, n_a_c_d_out, n_nb_nc_out, n_a_b_c_out);

  assign D_D = d;
  assign D_K = d;
endmodule
