// Logisim project BCD84-2-1 do kódu 3n+2.circ as structural Verilog: 1 circuit, main circuit main
module main (
  input  A,
  input  B,
  input  C,
  input  D,
  output A_DNF,
  output B_DNF,
  output C_DNF,
  output D_DNF,
  output E_DNF,
  output A_KNF,
  output B_KNF,
  output C_KNF,
  output D_KNF,
  output E_KNF
);

  wire a_nc_nd_2_out, a_nc_nd_out, a_ncd_out, ab_2_out, ab_out, ac_nd_out, b_nc_nd_2_out, b_nc_nd_out,
       b_nc_out, b_ncd_out, b_nd_2_out, b_nd_out, bcd_2_out, bcd_out, nb_ncd_out, nB_out, nbc_nd_out,
       nbd_out, nD_2_out, nD_out;

  nand nB (nB_out, B, B);
  nand nC (D_DNF, C, C);
  nor nC_2 (D_KNF, C, C);
  nand nD (nD_out, D, D);
  nor nD_2 (nD_2_out, D, D);
  and nbc_nd (nbc_nd_out, nB_out, C, nD_out);
  and a_nc_nd (a_nc_nd_out, A, D_DNF, nD_out);
  and nbd (nbd_out, nB_out, D);
  and ab (ab_out, A, B);
  and b_ncd (b_ncd_out, B, D_DNF, D);
  and b_nd (b_nd_out, B, nD_out);
  and nb_ncd (nb_ncd_out, nB_out, D_DNF, D);
  and b_nc_nd (b_nc_nd_out, B, D_DNF, nD_out);
  and bcd (bcd_out, D, C, B);
  nor ab_2 (ab_2_out, A, B);
  nor b_nd_2 (b_nd_2_out, B, nD_2_out);
  nor b_nc (b_nc_out, B, D_KNF);
  nor a_nc_nd_2 (a_nc_nd_2_out, A, D_KNF, nD_2_out);
  nor bcd_2 (bcd_2_out, B, C, D);
  nor ac_nd (ac_nd_out, A, C, nD_2_out);
  nor b_nc_nd_2 (b_nc_nd_2_out, B, D_KNF, nD_2_out);
  nor a_ncd (a_ncd_out, D, D_KNF, A);
  and u_A_DNF (A_DNF, nbc_nd_out, a_nc_nd_out, nbd_out, ab_out);
  and u_B_DNF (B_DNF, a_nc_nd_out, b_ncd_out, b_nd_out, ab_out);
  and u_C_DNF (C_DNF, nb_ncd_out, nbc_nd_out, b_nc_nd_out, bcd_out);
  and u_E_DNF (E_DNF, nbd_out, b_ncd_out, bcd_out);
  nor u_B_Knf (B_KNF, ab_2_out, b_nd_2_out, b_nc_out, a_nc_nd_2_out);
  nor u_C_Knf (C_KNF, bcd_2_out, ac_nd_out, b_nc_nd_2_out, a_ncd_out);

  assign A_KNF = A;
  assign E_KNF = D;

  // Notes on the sheet:
  //   DNF
  //   KNF
  //   DNF
  //   KNF
endmodule
