// Logisim project 011001.circ as structural Verilog: 1 circuit, main circuit main
module main (
  input  X,
  input  Res,
  output Y
);

  wire clock_1_out, J1_out, J2_out, J3_out, j_k_ff_1_q, j_k_ff_2_q, j_k_ff_2_qn, j_k_ff_3_q, j_k_ff_3_qn,
       K1_out, K2_out, K3_out, nX_out, nX_Z2_Z3_out, nX_Z3_out, X_Z1_nZ3_out, X_Z1_Z2_out, X_Z3_out;

  nand nX (nX_out, X, X);
  nand nX_Z2_Z3 (nX_Z2_Z3_out, nX_out, j_k_ff_2_q, j_k_ff_3_q);
  nand X_Z1_Z2 (X_Z1_Z2_out, X, j_k_ff_1_q, j_k_ff_2_q);
  nand X_Z1_nZ3 (X_Z1_nZ3_out, X, j_k_ff_1_q, j_k_ff_3_qn);
  nand nX_Z3 (nX_Z3_out, nX_out, j_k_ff_3_q);
  nand X_Z3 (X_Z3_out, X, j_k_ff_3_q);
  nand nand_1 (Y, X_Z1_Z2_out, X_Z1_Z2_out);
  nand J1 (J1_out, nX_Z2_Z3_out, nX_Z2_Z3_out);
  nand K1 (K1_out, nX_Z3_out, X_Z1_nZ3_out, j_k_ff_2_qn);
  nand J2 (J2_out, X_Z1_nZ3_out, X_Z3_out);
  nand K2 (K2_out, X_Z3_out, X);
  nand J3 (J3_out, j_k_ff_2_qn, X);
  nand K3 (K3_out, X_Z3_out, j_k_ff_2_qn);
  Clock clock_1 (.out(clock_1_out));
  J_K_Flip_Flop j_k_ff_1 (
    .J(J1_out), .clk(clock_1_out), .K(K1_out), .Q(j_k_ff_1_q), .reset(Res));  // open: Qn, preset, en
  J_K_Flip_Flop j_k_ff_2 (
    .J(J2_out), .clk(clock_1_out), .K(K2_out), .Q(j_k_ff_2_q), .Qn(j_k_ff_2_qn), .reset(Res));  // open: preset, en
  J_K_Flip_Flop j_k_ff_3 (
    .J(J3_out), .clk(clock_1_out), .K(K3_out), .Q(j_k_ff_3_q), .Qn(j_k_ff_3_qn), .reset(Res));  // open: preset, en

  // Notes on the sheet:
  //   Z1
  //   Z2
  //   Z3
  //   CLK
endmodule
